# Fritzing sketch loading (saved by Fritzing 0.9.3b)
breadboards: 1

parts:
  Bauteil1 = Arduino Nano (Rev3.0)
  Bauteil2 = Arduino Ethernet Shield (Rev3)
  IC1 = L293D [package=THT]
  Bauteil3 = RFID-RC522-v3
  Squix1 = OLED 0.96" 128x64 I2C SSD1306
  VCC1 = Battery block 9V
  J1 = Infrared Proximity Sensor
  J2 = Infrared Proximity Sensor
  J3 = Infrared Proximity Sensor
  J4 = Infrared Proximity Sensor
  J5 = Infrared Proximity Sensor
  J6 = Infrared Proximity Sensor
  M1 = DC Motor

nets:
  N1: Bauteil1.D1/TX, Bauteil2.RX/D0
  N2: Bauteil1.D0/RX, Bauteil2.TX/D1
  GND: Bauteil1.GND, Bauteil2.GND, IC1.0V, Bauteil3.GND, Squix1.GND, VCC1.-, J1.GND
  5V: Bauteil1.5V, Squix1.VCC
  N3: Bauteil1.A5, Squix1.SCL
  N4: Bauteil1.A4, Squix1.SCA
  N5: Bauteil2.D8, Bauteil3.SDA
  N6: Bauteil2.PWM_D9, Bauteil3.RST
  N7: Bauteil2.PWM_D11, Bauteil3.MOSI
  N8: Bauteil2.SPI/D12, Bauteil3.MISO
  N9: Bauteil2.SPI/D13, Bauteil3.SCK
  N10: Bauteil2.A0, J6.Vout
  N11: Bauteil2.A1, J5.Vout
  N12: Bauteil2.A2, J4.Vout
  N13: Bauteil2.A3, J3.Vout
  N14: Bauteil2.A4/SDA, J2.Vout
  N15: Bauteil2.A5/SCL, J1.Vout
  N16: Bauteil2.D2, IC1.In_2
  N17: Bauteil2.PWM_D3, IC1.Enable_1
  N18: Bauteil2.SDCS, IC1.In_1
  3V3: Bauteil2.3V3, Bauteil3.3.3V
  5V_2: Bauteil2.5V, IC1.+V, J1.Vcc
  N19: IC1.Out_1_(_Controlled_by_Enable_1_), M1.pin_2
  N20: IC1.Out_2_(_Controlled_by_Enable_1_), M1.pin_1
  N21: IC1.+Vmotor, VCC1.+

custom parts:
  RFID-RC522-v3: A simple China made RFID-RC522 Reader (6x4 cm); do check the pin labels, as this is a MFRC522 based clone.
