# Fritzing sketch quality (saved by Fritzing 0.9.3b)
breadboards: 1

parts:
  Bauteil1 = Arduino Nano (Rev3.0)
  Bauteil2 = Arduino Ethernet Shield (Rev3)
  IC1 = L293D [package=THT]
  Squix1 = OLED 0.96" 128x64 I2C SSD1306
  VCC1 = Battery block 9V
  J1 = Infrared Proximity Sensor
  J2 = Infrared Proximity Sensor
  J3 = Infrared Proximity Sensor
  J4 = Infrared Proximity Sensor
  J5 = Infrared Proximity Sensor
  J6 = Infrared Proximity Sensor
  M1 = DC Motor
  Bauteil3 = Arduino Ethernet Shield (Rev3)
  e-radionica1 = TCS230 Color Sensor [part_number=101209]
  Bauteil4 = Arduino Nano (Rev3.0)
  Squix2 = OLED 0.96" 128x64 I2C SSD1306

nets:
  N1: Bauteil1.D1/TX, Bauteil2.RX/D0
  N2: Bauteil1.D0/RX, Bauteil2.TX/D1
  GND: Bauteil1.GND, Bauteil2.GND, IC1.0V, Squix1.GND, VCC1.-, J1.GND
  5V: Bauteil1.5V, Squix1.VCC
  N3: Bauteil1.A5, Squix1.SCL
  N4: Bauteil1.A4, Squix1.SCA
  N5: Bauteil2.A0, J6.Vout
  N6: Bauteil2.A1, J5.Vout
  N7: Bauteil2.A2, J4.Vout
  N8: Bauteil2.A3, J3.Vout
  N9: Bauteil2.A4/SDA, J2.Vout
  N10: Bauteil2.A5/SCL, J1.Vout
  N11: Bauteil2.D2, IC1.In_2
  N12: Bauteil2.PWM_D3, IC1.Enable_1
  N13: Bauteil2.SDCS, IC1.In_1
  N14: Bauteil2.PWM_D5, IC1.Enable_2
  N15: Bauteil2.PWM_D6, IC1.In_3
  N16: Bauteil2.D7, IC1.In_4
  5V_2: Bauteil2.5V, IC1.+V, J1.Vcc
  N17: IC1.Out_1_(_Controlled_by_Enable_1_), M1.pin_2
  N18: IC1.Out_2_(_Controlled_by_Enable_1_), M1.pin_1
  N19: IC1.+Vmotor, VCC1.+
  N20: Bauteil3.D8, e-radionica1.Out
  N21: Bauteil3.RX/D0, Bauteil4.D1/TX
  N22: Bauteil3.TX/D1, Bauteil4.D0/RX
  N23: Bauteil3.SDCS, e-radionica1.S0
  N24: Bauteil3.PWM_D5, e-radionica1.S1
  N25: Bauteil3.PWM_D6, e-radionica1.S2
  N26: Bauteil3.D7, e-radionica1.S3
  5V_3: Bauteil3.5V, e-radionica1.Vcc
  GND_2: Bauteil3.GND, e-radionica1.Gnd
  GND_3: Bauteil4.GND, Squix2.GND
  5V_4: Bauteil4.5V, Squix2.VCC
  N27: Bauteil4.A5, Squix2.SCL
  N28: Bauteil4.A4, Squix2.SCA

custom parts:
  TCS230 Color Sensor: TCS230
