# Fritzing sketch unloading (saved by Fritzing 0.9.3b)
breadboards: 1

parts:
  Bauteil1 = Arduino Nano (Rev3.0)
  Bauteil2 = Arduino Ethernet Shield (Rev3)
  IC1 = L293D [package=THT]
  Squix1 = OLED 0.96" 128x64 I2C SSD1306
  VCC1 = Battery block 9V
  J1 = Infrared Proximity Sensor
  J2 = Infrared Proximity Sensor
  J3 = Infrared Proximity Sensor
  J4 = Infrared Proximity Sensor
  J5 = Infrared Proximity Sensor
  J6 = Infrared Proximity Sensor
  M1 = DC Motor
  M3 = DC Motor  # not connected

nets:
  N1: Bauteil1.D1/TX, Bauteil2.RX/D0
  N2: Bauteil1.D0/RX, Bauteil2.TX/D1
  GND: Bauteil1.GND, Bauteil2.GND, IC1.0V, Squix1.GND, VCC1.-, J1.GND
  5V: Bauteil1.5V, Squix1.VCC
  N3: Bauteil1.A5, Squix1.SCL
  N4: Bauteil1.A4, Squix1.SCA
  N5: Bauteil2.A0, J6.Vout
  N6: Bauteil2.A1, J5.Vout
  N7: Bauteil2.A2, J4.Vout
  N8: Bauteil2.A3, J3.Vout
  N9: Bauteil2.A4/SDA, J2.Vout
  N10: Bauteil2.A5/SCL, J1.Vout
  N11: Bauteil2.D2, IC1.In_2
  N12: Bauteil2.PWM_D3, IC1.Enable_1
  N13: Bauteil2.SDCS, IC1.In_1
  N14: Bauteil2.PWM_D5, IC1.Enable_2
  N15: Bauteil2.PWM_D6, IC1.In_3
  N16: Bauteil2.D7, IC1.In_4
  5V_2: Bauteil2.5V, IC1.+V, J1.Vcc
  N17: IC1.Out_1_(_Controlled_by_Enable_1_), M1.pin_2
  N18: IC1.Out_2_(_Controlled_by_Enable_1_), M1.pin_1
  N19: IC1.+Vmotor, VCC1.+
